# Fritzing sketch Projeto_ProtoboardMaior (saved by Fritzing 0.9.3b)
breadboards: 1

parts:
  NodeMCU_-_2 = NodeMCU V3.0
  DHT3 = DHT11 Humitidy and Temperature Sensor
  Power_plug3 = Power plug
  M3 = DC Motor
  KY-3 = Keyes Relay [package=THT]
  Componente3 = Soil Moisture Sensor
  NodeMCU_-_1 = NodeMCU V3.0  # not connected

nets:
  N1: NodeMCU_-_2.D2, KY-3.signal
  N2: NodeMCU_-_2.D3, DHT3.NULL
  N3: NodeMCU_-_2.GND#6, NodeMCU_-_2.GND#13, NodeMCU_-_2.GND#16, NodeMCU_-_2.GND#33, DHT3.GND
  VCC: NodeMCU_-_2.Vin, DHT3.VDD, Power_plug3.VCC, KY-3.power, KY-3.C, Componente3.VCC
  N4: NodeMCU_-_2.A0, Componente3.SIG
  GND: Power_plug3.GND, M3.pin_2, KY-3.ground, Componente3.GND
  N5: M3.pin_1, KY-3.NO

custom parts:
  NodeMCU V3.0: ESP8266 based NodeMCU
  DHT11 Humitidy and Temperature Sensor: DHT11 Humidity and Temperature Sensor
  Keyes Relay: The Keyes 5V relay module is suitable for SCM development, home appliance control. It uses a 5V~12V TIL control signal which can control DC / AC signal.
